# Fritzing sketch CubbyCube Midterm fritz (saved by Fritzing 0.9.9b)
breadboards: 3

parts:
  Breadboard4 = Breadboard Split Power
  Breadboard5 = Breadboard Split Power
  Teensy_3_1 = Teensy 3.1
  HC-SR04_Sensor_1 = HC-SR04 Ultrasonic Distance Sensor
  M1 = BMP280
  OLED_I2C1 = OLED 128x64 I2C Monochrome Display
  WIZ820io1 = WIZ820io [part_number=WIZ820io]
  Part1 = 4x4 Keypad [part_number=101207]

nets:
  3V3: Breadboard4.pin3Y, Breadboard4.pin15Y, Breadboard4.pin17Y, Breadboard4.pin22Y, Breadboard4.pin29Y, Breadboard5.pin3Y, Breadboard5.pin12Y, Breadboard5.pin15Y, Breadboard5.pin17Y, Teensy_3_1.3V3, M1.VIN, OLED_I2C1.VDD
  GND: Breadboard4.pin3Z, Breadboard4.pin19Z, Breadboard4.pin29Z, Breadboard5.pin3Z, Breadboard5.pin11Z, Breadboard5.pin29Z, Teensy_3_1.GND, HC-SR04_Sensor_1.GND, M1.GND, OLED_I2C1.GND, WIZ820io1.GND
  N1: Teensy_3_1.D6, HC-SR04_Sensor_1.ECHO
  N2: Teensy_3_1.D7, HC-SR04_Sensor_1.TRIG
  N3: Teensy_3_1.D9, WIZ820io1.nSS
  N4: Teensy_3_1.D11, WIZ820io1.MOSI
  N5: Teensy_3_1.D12, WIZ820io1.MISO
  N6: Teensy_3_1.D13, WIZ820io1.SCLK
  N7: Teensy_3_1.A0/D14, Part1.1
  N8: Teensy_3_1.A1/D15, Part1.2
  N9: Teensy_3_1.A2/D16, Part1.3
  N10: Teensy_3_1.A3/D17, Part1.4
  N11: Teensy_3_1.A4/D18, M1.SDA, OLED_I2C1.SDA
  N12: Teensy_3_1.A5/D19, M1.SCL, OLED_I2C1.SCK
  N13: Teensy_3_1.A6/D20, Part1.5
  N14: Teensy_3_1.A7/D21, Part1.6
  N15: Teensy_3_1.A8/D22, Part1.7
  N16: Teensy_3_1.A9/D23, Part1.8
  VIN: Teensy_3_1.Vin, HC-SR04_Sensor_1.VCC, WIZ820io1.VIN

custom parts:
  Breadboard Split Power: A custom 6 pin per group power supply strip where the top row (ground) is all bussed together and the bottom row (+V) is split in two groups of 12 pins. This version is modified to be a loadable part and was rescaled to be on the standard 1px = 1thou grid with the size set in inches
  BMP280: Temperature Humidity Barometric presure Sensor, I2C
  4x4 Keypad: Matrix membrane keypad 4x4
